// Logisim project FinalProjectCircuit.circ as structural Verilog: 4 circuits, main circuit DownCounter
module DownCounter (
  input  Clock,
  input  Enable,
  output out_3,
  output [3:0] out_4
);

  wire nor_1_out, s_r_ff_1_q, s_r_ff_1_qn;

  S_R_Flip_Flop s_r_ff_1 (
    .S(s_r_ff_1_qn), .R(s_r_ff_1_q), .clk(nor_1_out), .Q(s_r_ff_1_q), .Qn(s_r_ff_1_qn), .preset(Enable));  // open: reset
  T_Flip_Flop t_ff_1 (.T(s_r_ff_1_q), .clk(Clock), .Q(out_4[0]), .reset(Enable));  // open: Qn, preset
  nor nor_1 (nor_1_out, out_4[0], out_4[1], out_4[2], out_4[3]);
  T_Flip_Flop t_ff_2 (.T(s_r_ff_1_q), .clk(out_4[0]), .Q(out_4[1]), .preset(Enable));  // open: Qn, reset
  T_Flip_Flop t_ff_3 (.T(s_r_ff_1_q), .clk(out_4[1]), .Q(out_4[2]), .reset(Enable));  // open: Qn, preset
  T_Flip_Flop t_ff_4 (.T(s_r_ff_1_q), .clk(out_4[2]), .Q(out_4[3]), .preset(Enable));  // open: Qn, reset
  S_R_Flip_Flop s_r_ff_2 (.Q(out_3), .reset(Enable), .preset(nor_1_out));  // open: S, R, clk, Qn

  // Other names for the same wires on the sheet: Q0 = out_4[0]; Q1 = out_4[1]; Q2 = out_4[2]; Q3 = out_4[3]
endmodule

module Light1 (
  input  Press2Cross,
  input  Clk,
  output NXT_State,
  output [3:0] L1_Out,
  output [3:0] Cross_Counter,
  output [3:0] L2_Out
);

  wire Hold, L1_ZeroTracker, L2_ZeroTracker, Light1Enab, Light2Enab, nor_3_out, nor_4_out, or_1_out,
       s_r_ff_1_q, s_r_ff_1_qn, s_r_ff_2_q, s_r_ff_2_qn, s_r_ff_3_qn, t_ff_9_q, t_ff_12_q, t_ff_14_q,
       t_ff_14_qn;

  S_R_Flip_Flop s_r_ff_1 (
    .S(s_r_ff_1_qn), .R(s_r_ff_1_q), .clk(L1_ZeroTracker), .Q(s_r_ff_1_q), .Qn(s_r_ff_1_qn),
    .preset(Light1Enab));  // open: reset
  T_Flip_Flop t_ff_1 (.T(s_r_ff_1_q), .clk(Clk), .Q(L1_Out[0]), .preset(Light1Enab));  // open: Qn, reset
  S_R_Flip_Flop s_r_ff_2 (
    .S(s_r_ff_2_qn), .R(s_r_ff_2_q), .clk(L2_ZeroTracker), .Q(s_r_ff_2_q), .Qn(s_r_ff_2_qn),
    .preset(Light2Enab));  // open: reset
  T_Flip_Flop t_ff_2 (.T(s_r_ff_2_q), .clk(Clk), .Q(L2_Out[0]), .preset(Light2Enab));  // open: Qn, reset
  T_Flip_Flop t_ff_3 (.T(s_r_ff_1_q), .clk(L1_Out[0]), .Q(L1_Out[1]), .preset(Light1Enab));  // open: Qn, reset
  T_Flip_Flop t_ff_4 (.T(s_r_ff_2_q), .clk(L2_Out[0]), .Q(L2_Out[1]), .preset(Light2Enab));  // open: Qn, reset
  T_Flip_Flop t_ff_5 (.T(s_r_ff_1_q), .clk(L1_Out[1]), .Q(L1_Out[2]), .reset(Light1Enab));  // open: Qn, preset
  T_Flip_Flop t_ff_6 (.T(s_r_ff_2_q), .clk(L2_Out[1]), .Q(L2_Out[2]), .reset(Light2Enab));  // open: Qn, preset
  T_Flip_Flop t_ff_7 (.T(s_r_ff_1_q), .clk(L1_Out[2]), .Q(L1_Out[3]), .reset(Light1Enab));  // open: Qn, preset
  T_Flip_Flop t_ff_8 (.T(s_r_ff_2_q), .clk(L2_Out[2]), .Q(L2_Out[3]), .reset(Light2Enab));  // open: Qn, preset
  nor nor_1 (L1_ZeroTracker, L1_Out[3], L1_Out[2], L1_Out[1], L1_Out[0]);
  nor nor_2 (L2_ZeroTracker, L2_Out[3], L2_Out[2], L2_Out[1], L2_Out[0]);
  or or_1 (or_1_out, Light1Enab, Light2Enab);
  T_Flip_Flop t_ff_9 (.T(or_1_out), .clk(Clk), .Q(t_ff_9_q));  // open: Qn, reset, preset
  S_R_Flip_Flop s_r_ff_3 (
    .S(s_r_ff_3_qn), .R(Hold), .clk(nor_3_out), .Q(Hold), .Qn(s_r_ff_3_qn), .preset(Press2Cross));  // open: reset
  T_Flip_Flop t_ff_10 (.T(Hold), .clk(Clk), .Q(Cross_Counter[0]), .reset(Press2Cross));  // open: Qn, preset
  T_Flip_Flop t_ff_11 (
    .T(Hold), .clk(Cross_Counter[0]), .Q(Cross_Counter[1]), .preset(Press2Cross));  // open: Qn, reset
  T_Flip_Flop t_ff_12 (.T(or_1_out), .clk(t_ff_9_q), .Q(t_ff_12_q));  // open: Qn, reset, preset
  nor nor_3 (nor_3_out, Cross_Counter[0], Cross_Counter[1], Cross_Counter[2], Cross_Counter[3]);
  and and_1 (NXT_State, t_ff_9_q, t_ff_12_q);
  T_Flip_Flop t_ff_13 (
    .T(Hold), .clk(Cross_Counter[1]), .Q(Cross_Counter[2]), .reset(Press2Cross));  // open: Qn, preset
  T_Flip_Flop t_ff_14 (.T(nor_4_out), .clk(Clk), .Q(t_ff_14_q), .Qn(t_ff_14_qn));  // open: reset, preset
  nor nor_4 (nor_4_out, t_ff_12_q, t_ff_9_q);
  T_Flip_Flop t_ff_15 (
    .T(Hold), .clk(Cross_Counter[2]), .Q(Cross_Counter[3]), .preset(Press2Cross));  // open: Qn, reset
  nor nor_5 (Light1Enab, Hold, t_ff_14_q);
  nor nor_6 (Light2Enab, t_ff_14_qn, Hold);

  // Other names for the same wires on the sheet: Q0 = Cross_Counter[0]; Q1 = Cross_Counter[1]; Q2 = Cross_Counter[2];
  //   Q3 = Cross_Counter[3]
endmodule

module FSM_Final (
  input  Enab,
  input  NXT_ST,
  output Green,
  output Blue,
  output rst,
  output Red
);

  wire [1:0] multiplexer_1_out, register_1_q;

  Multiplexer #(.select(3), .width(2)) multiplexer_1 (
    .in0(2'b00), .in1(2'b01), .in2(2'b10), .in4(2'b01), .in5(2'b10), .in6(2'b00), .out(multiplexer_1_out),
    .sel({Enab, register_1_q}));  // open: in3, in7
  Register #(.width(2)) register_1 (.D(multiplexer_1_out), .Q(register_1_q), .clk(NXT_ST));  // open: en, clr
  // Probe on multiplexer_1_out
  and and_1 (Green, ~register_1_q[0], ~register_1_q[1]);  // AND_Gate
  and and_2 (Blue, register_1_q[0], ~register_1_q[1]);  // AND_Gate
  and and_3 (Red, ~register_1_q[0], register_1_q[1]);  // AND_Gate

  assign rst = NXT_ST;
endmodule

module Main_Final (
  input  En,
  input  Enable
);

  wire and_1_out, and_2_out, and_3_out, and_4_out, and_5_out, and_6_out, button_1_out, clk, G, G1, G2,
       n_state, Next_State, or_1_out, pedestrian_button_1_en, R, R1, R2, Y, Y1, Y2;
  wire [3:0] Countdown, DownCounter_v1_1_count, L1_Hex, L1_Out, L2_Hex, L2_Out;
  wire [7:0] bin2hex_1_hex0, bin2hex_1_hex1, bin2hex_2_hex0, bin2hex_2_hex1, bin2hex_3_hex0, bin2hex_3_hex1,
       HEX0, HEX1;

  Button button_1 (.out(button_1_out));
  and and_1 (and_1_out, ~DownCounter_v1_1_count[0], ~DownCounter_v1_1_count[1], ~DownCounter_v1_1_count[2], ~DownCounter_v1_1_count[3]);  // AND_Gate
  Clock u_clk (.out(clk));
  and and_2 (and_2_out, En, and_1_out);
  or or_1 (or_1_out, n_state, pedestrian_button_1_en);
  // RGBLED RGBLED_1: pin names not known; wires that end beside it: R
  // RGBLED RGBLED_2: pin names not known; wires that end beside it: Y, Y
  // RGBLED RGBLED_3: pin names not known; wires that end beside it: G
  Light1 light1_1 (
    .Press2Cross(Enable), .Clk(button_1_out), .NXT_State(Next_State), .L1_Out(L1_Out),
    .Cross_Counter(Countdown), .L2_Out(L2_Out));
  _7_Segment_Display #(.active("false")) u_7_segment_display_1 (
    .g(bin2hex_1_hex1[6]), .f(bin2hex_1_hex1[5]), .a(bin2hex_1_hex1[0]), .b(bin2hex_1_hex1[1]),
    .e(bin2hex_1_hex1[4]), .d(bin2hex_1_hex1[3]), .c(bin2hex_1_hex1[2]), .dp(bin2hex_1_hex1[7]));
  FSM_Final fsm_final_1 (.Enab(En), .NXT_ST(and_2_out), .Green(G), .Blue(Y), .rst(R), .Red(n_state));
  Bin2Hex bin2hex_1 (
    .v3(L1_Hex[3]), .v2(L1_Hex[2]), .v1(L1_Hex[1]), .v0(L1_Hex[0]), .HEX1(bin2hex_1_hex1),
    .HEX0(bin2hex_1_hex0));
  _7_Segment_Display #(.active("false")) u_7_segment_display_2 (
    .g(bin2hex_1_hex0[6]), .f(bin2hex_1_hex0[5]), .a(bin2hex_1_hex0[0]), .b(bin2hex_1_hex0[1]),
    .e(bin2hex_1_hex0[4]), .d(bin2hex_1_hex0[3]), .c(bin2hex_1_hex0[2]), .dp(bin2hex_1_hex0[7]));
  _7_Segment_Display #(.active("false")) L_7_Segment_Display_1 (
    .g(HEX1[6]), .f(HEX1[5]), .a(HEX1[0]), .b(HEX1[1]), .e(HEX1[4]), .d(HEX1[3]), .c(HEX1[2]), .dp(HEX1[7]));
  DownCounter_v1 DownCounter_v1_1 (.en(or_1_out), .clk(clk), .count(DownCounter_v1_1_count));
  pedestrian_button pedestrian_button_1 (.counter(DownCounter_v1_1_count), .en(pedestrian_button_1_en));
  _7_Segment_Display #(.active("false")) u_7_segment_display_3 (
    .g(bin2hex_2_hex1[6]), .f(bin2hex_2_hex1[5]), .a(bin2hex_2_hex1[0]), .b(bin2hex_2_hex1[1]),
    .e(bin2hex_2_hex1[4]), .d(bin2hex_2_hex1[3]), .c(bin2hex_2_hex1[2]), .dp(bin2hex_2_hex1[7]));
  Bin2Hex bin2hex_2 (
    .v3(Countdown[3]), .v2(Countdown[2]), .v1(Countdown[1]), .v0(Countdown[0]), .HEX1(bin2hex_2_hex1),
    .HEX0(bin2hex_2_hex0));
  _7_Segment_Display #(.active("false")) u_7_segment_display_4 (
    .g(bin2hex_2_hex0[6]), .f(bin2hex_2_hex0[5]), .a(bin2hex_2_hex0[0]), .b(bin2hex_2_hex0[1]),
    .e(bin2hex_2_hex0[4]), .d(bin2hex_2_hex0[3]), .c(bin2hex_2_hex0[2]), .dp(bin2hex_2_hex0[7]));
  _7_Segment_Display #(.active("false")) L_7_Segment_Display_2 (
    .g(HEX0[6]), .f(HEX0[5]), .a(HEX0[0]), .b(HEX0[1]), .e(HEX0[4]), .d(HEX0[3]), .c(HEX0[2]), .dp(HEX0[7]));
  and and_3 (and_3_out, ~L1_Hex[0], ~L1_Hex[1], ~L1_Hex[2], ~L1_Hex[3]);  // AND_Gate
  and and_4 (and_4_out, and_3_out, Enable);
  and and_5 (and_5_out, Enable, and_6_out);
  and and_6 (and_6_out, ~L1_Hex[0], ~L1_Hex[1], ~L1_Hex[2], ~L1_Hex[3]);  // AND_Gate
  Bin2Hex Bin2Hex_1_dup2 (
    .v3(DownCounter_v1_1_count[3]), .v2(DownCounter_v1_1_count[2]), .v1(DownCounter_v1_1_count[1]),
    .v0(DownCounter_v1_1_count[0]), .HEX1(HEX1), .HEX0(HEX0));
  _7_Segment_Display #(.active("false")) u_7_segment_display_5 (
    .g(bin2hex_3_hex1[6]), .f(bin2hex_3_hex1[5]), .a(bin2hex_3_hex1[0]), .b(bin2hex_3_hex1[1]),
    .e(bin2hex_3_hex1[4]), .d(bin2hex_3_hex1[3]), .c(bin2hex_3_hex1[2]), .dp(bin2hex_3_hex1[7]));
  Bin2Hex bin2hex_3 (
    .v3(L2_Hex[3]), .v2(L2_Hex[2]), .v1(L2_Hex[1]), .v0(L2_Hex[0]), .HEX1(bin2hex_3_hex1),
    .HEX0(bin2hex_3_hex0));
  _7_Segment_Display #(.active("false")) u_7_segment_display_6 (
    .g(bin2hex_3_hex0[6]), .f(bin2hex_3_hex0[5]), .a(bin2hex_3_hex0[0]), .b(bin2hex_3_hex0[1]),
    .e(bin2hex_3_hex0[4]), .d(bin2hex_3_hex0[3]), .c(bin2hex_3_hex0[2]), .dp(bin2hex_3_hex0[7]));
  FSM_Final fsm_final_2 (.Enab(and_4_out), .NXT_ST(Next_State), .Green(G1), .Blue(Y1), .Red(R1));  // open: rst
  FSM_Final fsm_final_3 (.Enab(and_5_out), .NXT_ST(Next_State), .Green(G2), .Blue(Y2), .Red(R2));  // open: rst

  // Notes on the sheet:
  //   Traffic Light A
  //   Counter Display
endmodule
