// Logisim project Lab_6_MarshallH.circ as structural Verilog: 14 circuits, main circuit main
module main (
);

  wire b0, b1, b2, b3, b4, b5, b6, c0, c1, c2, c3, c4, c5, c6, Clk_out, CrossButton_out;
  wire [3:0] downcounter_withclear_1_out_3;
  wire [7:7] Bin2Hex_1_hex0, Bin2Hex_1_hex1;

  Button CrossButton (.out(CrossButton_out));
  Clock Clk (.out(Clk_out));
  DownCounter_withClear downcounter_withclear_1 (
    .PressHereToCross(CrossButton_out), .Clk(Clk_out), .out_3(downcounter_withclear_1_out_3));
  _7_Segment_Display #(.active("false")) L_7_Segment_Display_3 (
    .g(b6), .f(b5), .a(b0), .b(b1), .e(b4), .d(b3), .c(b2), .dp(1'b1));
  _7_Segment_Display #(.active("false")) L_7_Segment_Display_4 (
    .g(c6), .f(c5), .a(c0), .b(c1), .e(c4), .d(c3), .c(c2), .dp(1'b1));
  Bin2Hex Bin2Hex_1 (
    .v3(downcounter_withclear_1_out_3[3]), .v2(downcounter_withclear_1_out_3[2]),
    .v1(downcounter_withclear_1_out_3[1]), .v0(downcounter_withclear_1_out_3[0]),
    .HEX1({Bin2Hex_1_hex1[7], b6, b5, b4, b3, b2, b1, b0}),
    .HEX0({Bin2Hex_1_hex0[7], c6, c5, c4, c3, c2, c1, c0}));

  // Notes on the sheet:
  //   Counter Display
endmodule

module Seg7_Decoder (
  input  i_m3,
  input  i_m2,
  input  i_m1,
  input  i_m0,
  output [7:0] o_seg
);

  wire and_1_out, and_2_out, and_3_out, and_4_out, and_5_out, and_6_out, and_7_out, and_8_out, and_9_out,
       and_10_out, and_11_out, and_12_out, and_13_out, and_14_out, and_15_out, and_16_out, and_17_out,
       and_18_out, and_19_out, and_20_out, and_21_out, and_22_out, and_23_out, not_1_out, not_2_out,
       not_3_out, not_4_out;

  not not_1 (not_1_out, i_m3);
  not not_2 (not_2_out, i_m2);
  not not_3 (not_3_out, i_m1);
  not not_4 (not_4_out, i_m0);
  and and_1 (and_1_out, not_1_out, not_2_out, not_3_out);
  and and_2 (and_2_out, not_1_out, i_m2, i_m1, i_m0);
  and and_3 (and_3_out, i_m3, not_2_out, i_m1);
  and and_4 (and_4_out, not_1_out, not_2_out, i_m0);
  and and_5 (and_5_out, not_1_out, not_2_out, i_m1);
  and and_6 (and_6_out, not_2_out, i_m1, i_m0);
  and and_7 (and_7_out, i_m3, i_m2, not_3_out);
  and and_8 (and_8_out, not_1_out, i_m2, not_3_out);
  and and_9 (and_9_out, i_m3, i_m2, i_m1);
  and and_10 (and_10_out, not_1_out, not_2_out, not_3_out, i_m0);
  and and_11 (and_11_out, not_1_out, i_m2, not_3_out, not_4_out);
  and and_12 (and_12_out, not_1_out, i_m2, i_m1, i_m0);
  and and_13 (and_13_out, i_m3, not_2_out, i_m1, i_m0);
  and and_14 (and_14_out, i_m3, i_m2, i_m1, not_4_out);
  and and_15 (and_15_out, not_1_out, not_2_out, i_m1, not_4_out);
  and and_16 (and_16_out, i_m3, i_m2, not_3_out, not_4_out);
  and and_17 (and_17_out, not_1_out, i_m2, not_3_out, i_m0);
  and and_18 (and_18_out, not_1_out, i_m2, i_m1, not_4_out);
  and and_19 (and_19_out, i_m3, i_m2, i_m1, i_m0);
  and and_20 (and_20_out, not_1_out, not_2_out, not_3_out, i_m0);
  and and_21 (and_21_out, not_1_out, i_m2, not_3_out, not_4_out);
  and and_22 (and_22_out, i_m3, not_2_out, i_m1, i_m0);
  and and_23 (and_23_out, i_m3, i_m2, i_m1, not_4_out);
  or or_1 (o_seg[6], and_1_out, and_2_out, and_3_out);
  or or_2 (o_seg[5], and_4_out, and_5_out, and_6_out, and_7_out);
  or or_3 (o_seg[4], i_m0, and_8_out, and_9_out);
  or or_4 (o_seg[3], and_10_out, and_11_out, and_12_out, and_13_out, and_14_out);
  or or_5 (o_seg[2], and_15_out, and_16_out);
  or or_6 (o_seg[1], and_17_out, and_18_out, and_19_out);
  or or_7 (o_seg[0], and_20_out, and_21_out, and_22_out, and_23_out);

  assign o_seg[7] = 1'b1;
endmodule

module CircuitA (
  input  i2,
  input  i1,
  input  i0,
  output o2,
  output o1,
  output o0
);

  not not_1 (o1, i1);
  and and_1 (o2, i2, i1);

  assign o0 = i0;
endmodule

module myComparator (
  input  v3,
  input  v2,
  input  v1,
  input  v0,
  output z
);

  wire and_1_out, and_2_out;

  and and_1 (and_1_out, v3, v1);
  and and_2 (and_2_out, v3, v2);
  or or_1 (z, and_1_out, and_2_out);
endmodule

module CircuitB (
  input  z,
  output s6,
  output s5,
  output s4,
  output s3,
  output s2,
  output s1,
  output s0
);


  assign s0 = z;
  assign s1 = 1'b0;
  assign s2 = 1'b0;
  assign s3 = z;
  assign s4 = z;
  assign s5 = z;
  assign s6 = 1'b1;
endmodule

module Bin2Hex (
  input  v3,
  input  v2,
  input  v1,
  input  v0,
  output [7:0] HEX1,
  output [7:0] HEX0
);

  wire z;

  myComparator myComparator_1 (.v3(v3), .v2(v2), .v1(v1), .v0(v0), .z(z));
  CircuitB CircuitB_1 (
    .z(z), .s6(HEX1[6]), .s5(HEX1[5]), .s4(HEX1[4]), .s3(HEX1[3]), .s2(HEX1[2]), .s1(HEX1[1]), .s0(HEX1[0]));
  Seg7_Decoder Seg7_Decoder_1 (.i_m3(v3), .i_m2(v2), .i_m1(v1), .i_m0(v0), .o_seg(HEX0));

  assign HEX1[7] = 1'b1;
endmodule

module UpCounter_Template (
  input  Enable,
  input  Clock,
  output [3:0] Output_bus_1
);

  wire t_ff_1_qn, t_ff_2_qn, t_ff_3_qn;

  T_Flip_Flop t_ff_1 (.T(Enable), .clk(Clock), .Q(Output_bus_1[0]), .Qn(t_ff_1_qn));  // open: reset, preset
  T_Flip_Flop t_ff_2 (.T(Enable), .clk(t_ff_1_qn), .Q(Output_bus_1[1]), .Qn(t_ff_2_qn));  // open: reset, preset
  T_Flip_Flop t_ff_3 (.T(Enable), .clk(t_ff_2_qn), .Q(Output_bus_1[2]), .Qn(t_ff_3_qn));  // open: reset, preset
  T_Flip_Flop t_ff_4 (.T(Enable), .clk(t_ff_3_qn), .Q(Output_bus_1[3]));  // open: Qn, reset, preset
endmodule

module DownCounter_Template (
  input  Enable,
  input  Clk,
  output [3:0] out_3
);

  T_Flip_Flop t_ff_1 (.T(Enable), .clk(Clk), .Q(out_3[0]));  // open: Qn, reset, preset
  T_Flip_Flop t_ff_2 (.T(Enable), .clk(out_3[0]), .Q(out_3[1]));  // open: Qn, reset, preset
  T_Flip_Flop t_ff_3 (.T(Enable), .clk(out_3[1]), .Q(out_3[2]));  // open: Qn, reset, preset
  T_Flip_Flop t_ff_4 (.T(Enable), .clk(out_3[2]), .Q(out_3[3]));  // open: Qn, reset, preset
endmodule

module Mod5_Template (
  input  Enable,
  input  Clock,
  output [3:0] out_3
);

  wire and_1_out, nand_1_out, not_1_out, not_2_out, not_3_out;

  T_Flip_Flop t_ff_1 (.T(Enable), .clk(Clock), .Q(out_3[0]), .reset(not_1_out));  // open: Qn, preset
  not not_1 (not_1_out, nand_1_out);
  T_Flip_Flop t_ff_2 (.T(out_3[0]), .clk(Clock), .Q(out_3[1]), .reset(not_2_out));  // open: Qn, preset
  not not_2 (not_2_out, nand_1_out);
  T_Flip_Flop t_ff_3 (.T(and_1_out), .clk(Clock), .Q(out_3[2]), .reset(not_3_out));  // open: Qn, preset
  and and_1 (and_1_out, out_3[0], out_3[1]);
  not not_3 (not_3_out, nand_1_out);
  nand nand_1 (nand_1_out, out_3[0], out_3[2]);
  T_Flip_Flop t_ff_4 ();  // open: T, clk, Q, Qn, reset, preset

  assign out_3[3] = 1'b0;

  // Other names for the same wires on the sheet: Q0 = out_3[0]; Q1 = out_3[1]; Q2 = out_3[2]
endmodule

module UpCounter_withClear (
  input  Enable,
  input  Clock,
  input  Clear_n,
  output [3:0] out_4
);

  wire and_1_out, and_2_out, and_3_out;

  T_Flip_Flop t_ff_1 (.T(Enable), .clk(Clock), .Q(out_4[0]), .reset(Clear_n));  // open: Qn, preset
  and and_1 (and_1_out, Enable, out_4[0]);
  T_Flip_Flop t_ff_2 (.T(and_1_out), .clk(Clock), .Q(out_4[1]), .reset(Clear_n));  // open: Qn, preset
  and and_2 (and_2_out, and_1_out, out_4[1]);
  T_Flip_Flop t_ff_3 (.T(and_2_out), .clk(Clock), .Q(out_4[2]), .reset(Clear_n));  // open: Qn, preset
  and and_3 (and_3_out, and_2_out, out_4[2]);
  T_Flip_Flop t_ff_4 (.T(and_3_out), .clk(Clock), .Q(out_4[3]), .reset(Clear_n));  // open: Qn, preset
endmodule

module JohnsonCounter (
  input  Clock,
  input  Reset,
  output [3:0] out_3
);

  wire d_ff_4_qn;

  D_Flip_Flop d_ff_1 (.D(d_ff_4_qn), .clk(Clock), .Q(out_3[0]), .reset(Reset));  // open: Qn, preset
  D_Flip_Flop d_ff_2 (.D(out_3[0]), .clk(Clock), .Q(out_3[1]), .reset(Reset));  // open: Qn, preset
  D_Flip_Flop d_ff_3 (.D(out_3[1]), .clk(Clock), .Q(out_3[2]), .reset(Reset));  // open: Qn, preset
  D_Flip_Flop d_ff_4 (.D(out_3[2]), .clk(Clock), .Q(out_3[3]), .Qn(d_ff_4_qn), .reset(Reset));  // open: preset
endmodule

module DownCounter_withClear (
  input  PressHereToCross,
  input  Clk,
  output [3:0] out_3
);

  wire button_1_out, nor_1_out, s_r_ff_1_q, s_r_ff_1_qn, undriven, undriven_2, undriven_3;
  wire [3:0] t_ff_1_q, t_ff_2_q;

  Button button_1 (.out(button_1_out));
  T_Flip_Flop t_ff_1 (.T(undriven), .Q(t_ff_1_q[0]), .preset(button_1_out));  // open: clk, Qn, reset
  T_Flip_Flop t_ff_2 (.T(undriven_2), .Q(t_ff_2_q[0]), .reset(undriven_3));  // open: clk, Qn, preset
  T_Flip_Flop t_ff_3 (.T(undriven), .clk(t_ff_1_q[0]), .Q(t_ff_1_q[1]));  // open: Qn, reset, preset
  T_Flip_Flop t_ff_4 (.T(undriven_2), .clk(t_ff_2_q[0]), .Q(t_ff_2_q[1]), .preset(undriven_3));  // open: Qn, reset
  T_Flip_Flop t_ff_5 (.T(s_r_ff_1_q), .clk(Clk), .Q(out_3[0]), .reset(PressHereToCross));  // open: Qn, preset
  S_R_Flip_Flop s_r_ff_1 (
    .S(s_r_ff_1_qn), .R(s_r_ff_1_q), .clk(nor_1_out), .Q(s_r_ff_1_q), .Qn(s_r_ff_1_qn),
    .preset(PressHereToCross));  // open: reset
  T_Flip_Flop t_ff_6 (.T(undriven), .clk(t_ff_1_q[1]), .Q(t_ff_1_q[2]), .preset(button_1_out));  // open: Qn, reset
  T_Flip_Flop t_ff_7 (.T(undriven_2), .clk(t_ff_2_q[1]), .Q(t_ff_2_q[2]), .reset(undriven_3));  // open: Qn, preset
  T_Flip_Flop t_ff_8 (.T(s_r_ff_1_q), .clk(out_3[0]), .Q(out_3[1]), .preset(PressHereToCross));  // open: Qn, reset
  T_Flip_Flop t_ff_9 (.T(undriven), .clk(t_ff_1_q[2]), .Q(t_ff_1_q[3]));  // open: Qn, reset, preset
  T_Flip_Flop t_ff_10 (.T(undriven_2), .clk(t_ff_2_q[2]), .Q(t_ff_2_q[3]), .preset(undriven_3));  // open: Qn, reset
  T_Flip_Flop t_ff_11 (.T(s_r_ff_1_q), .clk(out_3[1]), .Q(out_3[2]), .reset(PressHereToCross));  // open: Qn, preset
  T_Flip_Flop t_ff_12 (.T(s_r_ff_1_q), .clk(out_3[2]), .Q(out_3[3]), .preset(PressHereToCross));  // open: Qn, reset
  nor nor_1 (nor_1_out, out_3[3], out_3[2], out_3[1], out_3[0]);

  // Notes on the sheet:
  //   This counted down from 15.
  //   Also need a way for it to recognize when it hits 0
  //   Switch which flip flops the button goes into Sum. Was on 0 and 2, now on 1 and 3.
  //   Have the button reset bits 0 and 2 to make it start at 1010, or 10 in decimal
  //   Need to add a way that keeps track of start and doesnt restart until button pressed again
  //   The problem is that it does not stop after it gets to 0. It starts at 15 and goes down from there
  //   Messed around with SR flip-flop wiring into itself until I got here. IT WORKS!
  //   ZeroTracker
endmodule

module ShiftRegister (
  input  Input,
  input  Clock,
  output [3:0] out_3
);

  D_Flip_Flop d_ff_1 (.D(Input), .clk(Clock), .Q(out_3[0]));  // open: Qn, preset, reset
  D_Flip_Flop d_ff_2 (.D(out_3[0]), .clk(Clock), .Q(out_3[1]));  // open: Qn, preset, reset
  D_Flip_Flop d_ff_3 (.D(out_3[1]), .clk(Clock), .Q(out_3[2]));  // open: Qn, preset, reset
  D_Flip_Flop d_ff_4 (.D(out_3[2]), .clk(Clock), .Q(out_3[3]));  // open: Qn, preset, reset
endmodule

module ShiftWithMux (
  input  Set_Load,
  input  Serial_Input,
  input  Clock,
  input  [3:0] in_4,
  input  Reset,
  output [3:0] out_6
);

  wire multiplexer_1_out, multiplexer_2_out, multiplexer_3_out, multiplexer_4_out;

  Multiplexer multiplexer_1 (.in0(Serial_Input), .in1(in_4[3]), .out(multiplexer_1_out), .sel(Set_Load));
  D_Flip_Flop d_ff_1 (.D(multiplexer_1_out), .clk(Clock), .Q(out_6[3]), .reset(Reset));  // open: Qn, preset
  D_Flip_Flop d_ff_2 (.D(multiplexer_2_out), .clk(Clock), .Q(out_6[2]), .reset(Reset));  // open: Qn, preset
  Multiplexer multiplexer_2 (.in0(out_6[3]), .in1(in_4[2]), .out(multiplexer_2_out), .sel(Set_Load));
  D_Flip_Flop d_ff_3 (.D(multiplexer_3_out), .clk(Clock), .Q(out_6[1]), .reset(Reset));  // open: Qn, preset
  Multiplexer multiplexer_3 (.in0(out_6[2]), .in1(in_4[1]), .out(multiplexer_3_out), .sel(Set_Load));
  D_Flip_Flop d_ff_4 (.D(multiplexer_4_out), .clk(Clock), .Q(out_6[0]), .reset(Reset));  // open: Qn, preset
  Multiplexer multiplexer_4 (.in0(out_6[1]), .in1(in_4[0]), .out(multiplexer_4_out), .sel(Set_Load));
endmodule
