// Logisim project Lab8.circ as structural Verilog: 1 circuit, main circuit main
module main (
  input  Input_1,
  output R,
  output G,
  output B
);

  wire clock_1_out;

  T_Flip_Flop t_ff_1 (.T(Input_1), .clk(clock_1_out), .Q(R));  // open: Qn, reset, preset
  Clock clock_1 (.out(clock_1_out));
  T_Flip_Flop t_ff_2 (.T(Input_1), .clk(R), .Q(G));  // open: Qn, reset, preset
  T_Flip_Flop t_ff_3 (.T(Input_1), .clk(G), .Q(B));  // open: Qn, reset, preset
endmodule
